// Logisim project MIPS_Pipeline.circ as structural Verilog: 15 circuits, main circuit MIPS_Pipeline
module Instruction_Register (
  input  [31:0] in_1,
  input  Enable,
  input  Reset,
  input  Clock,
  output [5:0] _31_26,
  output [4:0] _25_21,
  output [4:0] _20_16,
  output [4:0] _15_11,
  output [15:0] _15_0
);

  Register #(.width(32)) register_1 (
    .D(in_1), .en(Enable), .Q({_31_26, _25_21, _20_16, _15_0}), .clk(Clock), .clr(Reset));

  assign _15_11 = _15_0[15:11];
endmodule

module Register_Bank (
  input  [4:0] Read_1_Address,
  input  [4:0] Read_2_Address,
  input  [4:0] Write_Address,
  input  [31:0] Write_Data,
  input  [31:0] Remainder,
  input  Enable,
  input  Reset,
  input  Clock,
  input  Division,
  output [31:0] Read_Data_1,
  output [31:0] Read_Data_2,
  output [31:0] High,
  output [31:0] Low
);

  wire and_1_out, and_2_out, and_3_out, and_4_out, and_5_out, and_6_out, and_7_out, and_8_out, and_9_out,
       and_10_out, and_11_out, and_12_out, and_13_out, and_14_out, and_15_out, and_16_out, and_17_out,
       and_18_out, and_19_out, and_20_out, and_21_out, and_22_out, and_23_out, and_24_out, and_25_out,
       and_26_out, and_27_out, and_28_out, and_29_out, and_30_out, and_31_out, and_32_out, and_33_out,
       dec_5_1_1_out_2, dec_5_1_1_out_3, dec_5_1_1_out_4, dec_5_1_1_out_5, dec_5_1_1_out_6, dec_5_1_1_out_7,
       dec_5_1_1_out_8, dec_5_1_1_out_9, dec_5_1_1_out_10, dec_5_1_1_out_11, dec_5_1_1_out_12,
       dec_5_1_1_out_13, dec_5_1_1_out_14, dec_5_1_1_out_15, dec_5_1_1_out_16, dec_5_1_1_out_17,
       dec_5_1_1_out_18, dec_5_1_1_out_19, dec_5_1_1_out_20, dec_5_1_1_out_21, dec_5_1_1_out_22,
       dec_5_1_1_out_23, dec_5_1_1_out_24, dec_5_1_1_out_25, dec_5_1_1_out_26, dec_5_1_1_out_27,
       dec_5_1_1_out_28, dec_5_1_1_out_29, dec_5_1_1_out_30, dec_5_1_1_out_31, dec_5_1_1_out_32,
       dec_5_1_1_out_33;
  wire [31:0] multiplexer_1_out, multiplexer_2_out, multiplexer_3_out, multiplexer_4_out, register_2_q,
       register_3_q, register_4_q, register_5_q, register_6_q, register_7_q, register_8_q, register_9_q,
       register_10_q, register_11_q, register_12_q, register_13_q, register_14_q, register_15_q,
       register_16_q, register_17_q, register_18_q, register_19_q, register_20_q, register_21_q,
       register_22_q, register_23_q, register_24_q, register_25_q, register_26_q, register_27_q,
       register_28_q, register_29_q, register_30_q, register_31_q, register_32_q;

  Dec_5_1 dec_5_1_1 (
    .in_1(Write_Address), .out_2(dec_5_1_1_out_2), .out_3(dec_5_1_1_out_3), .out_4(dec_5_1_1_out_4),
    .out_5(dec_5_1_1_out_5), .out_6(dec_5_1_1_out_6), .out_7(dec_5_1_1_out_7), .out_8(dec_5_1_1_out_8),
    .out_9(dec_5_1_1_out_9), .out_10(dec_5_1_1_out_10), .out_11(dec_5_1_1_out_11), .out_12(dec_5_1_1_out_12),
    .out_13(dec_5_1_1_out_13), .out_14(dec_5_1_1_out_14), .out_15(dec_5_1_1_out_15),
    .out_16(dec_5_1_1_out_16), .out_17(dec_5_1_1_out_17), .out_18(dec_5_1_1_out_18),
    .out_19(dec_5_1_1_out_19), .out_20(dec_5_1_1_out_20), .out_21(dec_5_1_1_out_21),
    .out_22(dec_5_1_1_out_22), .out_23(dec_5_1_1_out_23), .out_24(dec_5_1_1_out_24),
    .out_25(dec_5_1_1_out_25), .out_26(dec_5_1_1_out_26), .out_27(dec_5_1_1_out_27),
    .out_28(dec_5_1_1_out_28), .out_29(dec_5_1_1_out_29), .out_30(dec_5_1_1_out_30),
    .out_31(dec_5_1_1_out_31), .out_32(dec_5_1_1_out_32), .out_33(dec_5_1_1_out_33));
  and and_1 (and_1_out, dec_5_1_1_out_2, Enable);
  and and_2 (and_2_out, dec_5_1_1_out_3, Enable);
  and and_3 (and_3_out, dec_5_1_1_out_4, Enable);
  and and_4 (and_4_out, dec_5_1_1_out_5, Enable);
  and and_5 (and_5_out, dec_5_1_1_out_6, Enable);
  and and_6 (and_6_out, dec_5_1_1_out_7, Enable);
  and and_7 (and_7_out, dec_5_1_1_out_8, Enable);
  and and_8 (and_8_out, dec_5_1_1_out_9, Enable);
  and and_9 (and_9_out, dec_5_1_1_out_10, Enable);
  and and_10 (and_10_out, dec_5_1_1_out_11, Enable);
  and and_11 (and_11_out, dec_5_1_1_out_12, Enable);
  and and_12 (and_12_out, dec_5_1_1_out_13, Enable);
  and and_13 (and_13_out, dec_5_1_1_out_14, Enable);
  and and_14 (and_14_out, dec_5_1_1_out_15, Enable);
  and and_15 (and_15_out, dec_5_1_1_out_16, Enable);
  and and_16 (and_16_out, dec_5_1_1_out_17, Enable);
  and and_17 (and_17_out, dec_5_1_1_out_18, Enable);
  and and_18 (and_18_out, dec_5_1_1_out_19, Enable);
  and and_19 (and_19_out, dec_5_1_1_out_20, Enable);
  and and_20 (and_20_out, dec_5_1_1_out_21, Enable);
  and and_21 (and_21_out, dec_5_1_1_out_22, Enable);
  and and_22 (and_22_out, dec_5_1_1_out_23, Enable);
  and and_23 (and_23_out, dec_5_1_1_out_24, Enable);
  and and_24 (and_24_out, dec_5_1_1_out_25, Enable);
  and and_25 (and_25_out, dec_5_1_1_out_26, Enable);
  and and_26 (and_26_out, dec_5_1_1_out_27, Enable);
  and and_27 (and_27_out, dec_5_1_1_out_28, Enable);
  and and_28 (and_28_out, dec_5_1_1_out_29, Enable);
  and and_29 (and_29_out, dec_5_1_1_out_30, Enable);
  and and_30 (and_30_out, dec_5_1_1_out_31, Enable);
  and and_31 (and_31_out, dec_5_1_1_out_32, Enable);
  and and_32 (and_32_out, dec_5_1_1_out_33, Enable);
  and and_33 (and_33_out, Division, Enable);
  Register #(.width(32)) register_1 (.D(Write_Data), .en(and_1_out), .clk(Clock), .clr(Reset));  // open: Q
  Register #(.width(32)) register_2 (.D(Write_Data), .en(and_2_out), .Q(register_2_q), .clk(Clock), .clr(Reset));
  Register #(.width(32)) register_3 (.D(Write_Data), .en(and_3_out), .Q(register_3_q), .clk(Clock), .clr(Reset));
  Register #(.width(32)) register_4 (.D(Write_Data), .en(and_4_out), .Q(register_4_q), .clk(Clock), .clr(Reset));
  Register #(.width(32)) register_5 (.D(Write_Data), .en(and_5_out), .Q(register_5_q), .clk(Clock), .clr(Reset));
  Register #(.width(32)) register_6 (.D(Write_Data), .en(and_6_out), .Q(register_6_q), .clk(Clock), .clr(Reset));
  Register #(.width(32)) register_7 (.D(Write_Data), .en(and_7_out), .Q(register_7_q), .clk(Clock), .clr(Reset));
  Register #(.width(32)) register_8 (.D(Write_Data), .en(and_8_out), .Q(register_8_q), .clk(Clock), .clr(Reset));
  Register #(.width(32)) register_9 (.D(Write_Data), .en(and_9_out), .Q(register_9_q), .clk(Clock), .clr(Reset));
  Register #(.width(32)) register_10 (.D(Write_Data), .en(and_10_out), .Q(register_10_q), .clk(Clock), .clr(Reset));
  Register #(.width(32)) register_11 (.D(Write_Data), .en(and_11_out), .Q(register_11_q), .clk(Clock), .clr(Reset));
  Register #(.width(32)) register_12 (.D(Write_Data), .en(and_12_out), .Q(register_12_q), .clk(Clock), .clr(Reset));
  Register #(.width(32)) register_13 (.D(Write_Data), .en(and_13_out), .Q(register_13_q), .clk(Clock), .clr(Reset));
  Register #(.width(32)) register_14 (.D(Write_Data), .en(and_14_out), .Q(register_14_q), .clk(Clock), .clr(Reset));
  Register #(.width(32)) register_15 (.D(Write_Data), .en(and_15_out), .Q(register_15_q), .clk(Clock), .clr(Reset));
  Register #(.width(32)) register_16 (.D(Write_Data), .en(and_16_out), .Q(register_16_q), .clk(Clock), .clr(Reset));
  Register #(.width(32)) register_17 (.D(Write_Data), .en(and_17_out), .Q(register_17_q), .clk(Clock), .clr(Reset));
  Register #(.width(32)) register_18 (.D(Write_Data), .en(and_18_out), .Q(register_18_q), .clk(Clock), .clr(Reset));
  Register #(.width(32)) register_19 (.D(Write_Data), .en(and_19_out), .Q(register_19_q), .clk(Clock), .clr(Reset));
  Register #(.width(32)) register_20 (.D(Write_Data), .en(and_20_out), .Q(register_20_q), .clk(Clock), .clr(Reset));
  Register #(.width(32)) register_21 (.D(Write_Data), .en(and_21_out), .Q(register_21_q), .clk(Clock), .clr(Reset));
  Register #(.width(32)) register_22 (.D(Write_Data), .en(and_22_out), .Q(register_22_q), .clk(Clock), .clr(Reset));
  Register #(.width(32)) register_23 (.D(Write_Data), .en(and_23_out), .Q(register_23_q), .clk(Clock), .clr(Reset));
  Register #(.width(32)) register_24 (.D(Write_Data), .en(and_24_out), .Q(register_24_q), .clk(Clock), .clr(Reset));
  Register #(.width(32)) register_25 (.D(Write_Data), .en(and_25_out), .Q(register_25_q), .clk(Clock), .clr(Reset));
  Register #(.width(32)) register_26 (.D(Write_Data), .en(and_26_out), .Q(register_26_q), .clk(Clock), .clr(Reset));
  Register #(.width(32)) register_27 (.D(Write_Data), .en(and_27_out), .Q(register_27_q), .clk(Clock), .clr(Reset));
  Register #(.width(32)) register_28 (.D(Write_Data), .en(and_28_out), .Q(register_28_q), .clk(Clock), .clr(Reset));
  Register #(.width(32)) register_29 (.D(Write_Data), .en(and_29_out), .Q(register_29_q), .clk(Clock), .clr(Reset));
  Register #(.width(32)) register_30 (.D(Write_Data), .en(and_30_out), .Q(register_30_q), .clk(Clock), .clr(Reset));
  Register #(.width(32)) register_31 (.D(Write_Data), .en(and_31_out), .Q(register_31_q), .clk(Clock), .clr(Reset));
  Register #(.width(32)) register_32 (.D(Write_Data), .en(and_32_out), .Q(register_32_q), .clk(Clock), .clr(Reset));
  Register #(.width(32)) register_33 (.D(Remainder), .en(and_33_out), .Q(High), .clk(Clock), .clr(Reset));
  Register #(.width(32)) register_34 (.D(Write_Data), .en(and_33_out), .Q(Low), .clk(Clock), .clr(Reset));
  Multiplexer #(.select(4), .width(32), .enable("false")) multiplexer_1 (
    .in0({32{1'b0}}), .in1(register_2_q), .in2(register_3_q), .in3(register_4_q), .in4(register_5_q),
    .in5(register_6_q), .in6(register_7_q), .in7(register_8_q), .in8(register_9_q), .in9(register_10_q),
    .in10(register_11_q), .in11(register_12_q), .in12(register_13_q), .in13(register_14_q),
    .in14(register_15_q), .in15(register_16_q), .out(multiplexer_1_out), .sel(Read_2_Address[3:0]));
  Multiplexer #(.select(4), .width(32), .enable("false")) multiplexer_2 (
    .in0({32{1'b0}}), .in1(register_2_q), .in2(register_3_q), .in3(register_4_q), .in4(register_5_q),
    .in5(register_6_q), .in6(register_7_q), .in7(register_8_q), .in8(register_9_q), .in9(register_10_q),
    .in10(register_11_q), .in11(register_12_q), .in12(register_13_q), .in13(register_14_q),
    .in14(register_15_q), .in15(register_16_q), .out(multiplexer_2_out), .sel(Read_1_Address[3:0]));
  Multiplexer #(.select(4), .width(32), .enable("false")) multiplexer_3 (
    .in0(register_17_q), .in1(register_18_q), .in2(register_19_q), .in3(register_20_q), .in4(register_21_q),
    .in5(register_22_q), .in6(register_23_q), .in7(register_24_q), .in8(register_25_q), .in9(register_26_q),
    .in10(register_27_q), .in11(register_28_q), .in12(register_29_q), .in13(register_30_q),
    .in14(register_31_q), .in15(register_32_q), .out(multiplexer_3_out), .sel(Read_1_Address[3:0]));
  Multiplexer #(.select(4), .width(32), .enable("false")) multiplexer_4 (
    .in0(register_17_q), .in1(register_18_q), .in2(register_19_q), .in3(register_20_q), .in4(register_21_q),
    .in5(register_22_q), .in6(register_23_q), .in7(register_24_q), .in8(register_25_q), .in9(register_26_q),
    .in10(register_27_q), .in11(register_28_q), .in12(register_29_q), .in13(register_30_q),
    .in14(register_31_q), .in15(register_32_q), .out(multiplexer_4_out), .sel(Read_2_Address[3:0]));
  Multiplexer #(.width(32), .enable("false")) multiplexer_5 (
    .in0(multiplexer_2_out), .in1(multiplexer_3_out), .out(Read_Data_1), .sel(Read_1_Address[4]));
  Multiplexer #(.width(32), .enable("false")) multiplexer_6 (
    .in0(multiplexer_1_out), .in1(multiplexer_4_out), .out(Read_Data_2), .sel(Read_2_Address[4]));
endmodule

module Dec_5_1 (
  input  [4:0] in_1,
  output out_2,
  output out_3,
  output out_4,
  output out_5,
  output out_6,
  output out_7,
  output out_8,
  output out_9,
  output out_10,
  output out_11,
  output out_12,
  output out_13,
  output out_14,
  output out_15,
  output out_16,
  output out_17,
  output out_18,
  output out_19,
  output out_20,
  output out_21,
  output out_22,
  output out_23,
  output out_24,
  output out_25,
  output out_26,
  output out_27,
  output out_28,
  output out_29,
  output out_30,
  output out_31,
  output out_32,
  output out_33
);

  wire decoder_1_out0, decoder_2_out0, not_1_out, not_2_out, not_3_out, not_4_out;
  wire [3:0] and_1_out, and_5_out;

  not not_1 (not_1_out, in_1[4]);
  not not_2 (not_2_out, in_1[4]);
  not not_3 (not_3_out, in_1[4]);
  not not_4 (not_4_out, in_1[4]);
  and and_1 (and_1_out[0], not_1_out, in_1[0]);
  and and_2 (and_1_out[1], not_2_out, in_1[1]);
  and and_3 (and_1_out[2], not_3_out, in_1[2]);
  and and_4 (and_1_out[3], not_4_out, in_1[3]);
  and and_5 (and_5_out[0], in_1[4], in_1[0]);
  and and_6 (and_5_out[1], in_1[4], in_1[1]);
  and and_7 (and_5_out[2], in_1[4], in_1[2]);
  and and_8 (and_5_out[3], in_1[4], in_1[3]);
  Decoder #(.select(4), .enable("false")) decoder_1 (
    .out0(decoder_1_out0), .out1(out_3), .out2(out_4), .out3(out_5), .out4(out_6), .out5(out_7),
    .out6(out_8), .out7(out_9), .out8(out_10), .out9(out_11), .out10(out_12), .out11(out_13), .out12(out_14),
    .out13(out_15), .out14(out_16), .out15(out_17), .sel(and_1_out));
  Decoder #(.select(4), .enable("false")) decoder_2 (
    .out0(decoder_2_out0), .out1(out_19), .out2(out_20), .out3(out_21), .out4(out_22), .out5(out_23),
    .out6(out_24), .out7(out_25), .out8(out_26), .out9(out_27), .out10(out_28), .out11(out_29),
    .out12(out_30), .out13(out_31), .out14(out_32), .out15(out_33), .sel(and_5_out));
  and and_9 (out_2, not_1_out, decoder_1_out0);
  and and_10 (out_18, in_1[4], decoder_2_out0);
endmodule

module ALU (
  input  [31:0] Operand_1,
  input  [31:0] Operand_2,
  input  [2:0] Control,
  output Zero,
  output [31:0] Result,
  output [31:0] Remainder
);

  wire bitselector_1_out, not_1_out, or_2_out, or_3_out, or_4_out, or_5_out, or_6_out;
  wire [31:0] adder_1_out, and_1_out, bit_extender_1_out, divider_1_out, or_1_out, subtractor_1_out;

  assign and_1_out = Operand_1 & Operand_2;  // AND_Gate and_1, 32 bits wide
  assign or_1_out = Operand_1 | Operand_2;  // OR_Gate or_1, 32 bits wide
  Adder #(.width(32)) adder_1 (.a(Operand_1), .b(Operand_2), .out(adder_1_out));  // open: cin, cout
  Divider #(.width(32)) divider_1 (.a(Operand_1), .b(Operand_2), .out(divider_1_out), .rem(Remainder));  // open: upper
  BitSelector #(.width(32)) bitselector_1 (.in(Operand_1), .out(bitselector_1_out), .sel({5{1'b1}}));
  not not_1 (not_1_out, bitselector_1_out);
  Subtractor #(.width(32)) subtractor_1 (.a(Operand_1), .b(Operand_2), .out(subtractor_1_out));  // open: bin, bout
  assign bit_extender_1_out = {{31{1'b0}}, not_1_out};  // Bit_Extender bit_extender_1
  Multiplexer #(.select(3), .width(32), .enable("false")) multiplexer_1 (
    .in0(and_1_out), .in1(or_1_out), .in2(adder_1_out), .in3(divider_1_out), .in4(bit_extender_1_out),
    .in6(subtractor_1_out), .in7({{31{1'b0}}, subtractor_1_out[31]}), .out(Result), .sel(Control));  // open: in5
  or or_2 (or_2_out, Result[0], Result[1], Result[2], Result[3], Result[4], Result[5], Result[6], Result[7], Result[8]);
  or or_3 (or_3_out, Result[9], Result[10], Result[11], Result[12], Result[13], Result[14], Result[15], Result[16], Result[17]);
  or or_4 (or_4_out, Result[18], Result[19], Result[20], Result[21], Result[22], Result[23], Result[24], Result[25], Result[26]);
  or or_5 (or_5_out, Result[27], Result[28], Result[29], Result[30], Result[31]);
  or or_6 (or_6_out, or_2_out, or_3_out, or_4_out, or_5_out);
  not not_2 (Zero, or_6_out);
endmodule

module shl_26_28 (
  input  [25:0] in_1,
  output [27:0] out_2
);


  assign out_2 = {in_1, 2'b00};
endmodule

module merge_PC (
  input  [27:0] in_1,
  input  [3:0] in_2,
  output [31:0] out_3
);


  assign out_3 = {in_2, in_1};
endmodule

module sig_ext (
  input  [15:0] in_1,
  output [31:0] out_2
);


  assign out_2 = {{17{in_1[15]}}, in_1[14:0]};
endmodule

module shl_32 (
  input  [31:0] in_1,
  output [31:0] out_2
);


  assign out_2 = {in_1[29:0], 2'b00};
endmodule

module ALU_Control (
  input  [1:0] ALUop,
  input  [31:0] Input_Operand_1,
  input  [31:0] Input_Operand_2,
  input  [5:0] OPcode,
  input  [31:0] Offset,
  output [2:0] Result,
  output Division,
  output [31:0] ALU_Operand_1,
  output [31:0] ALU_Operand_2
);

  wire not_1_out, not_2_out, not_3_out, not_5_out, not_6_out, not_7_out, not_8_out;
  wire [2:0] or_1_out;
  wire [2:2] and_3_out;

  not not_1 (not_1_out, Offset[2]);
  not not_2 (not_2_out, Offset[0]);
  not not_3 (not_3_out, Offset[4]);
  and and_1 (Division, Offset[4], Offset[3], not_1_out, Offset[1], not_2_out);
  and and_2 (or_1_out[2], not_3_out, Offset[1]);
  not not_4 (or_1_out[1], Offset[2]);
  or or_1 (or_1_out[0], Offset[3], Offset[0]);
  not not_5 (not_5_out, OPcode[4]);
  not not_6 (not_6_out, OPcode[3]);
  not not_7 (not_7_out, OPcode[1]);
  not not_8 (not_8_out, OPcode[0]);
  Multiplexer #(.width(32), .enable("false")) multiplexer_1 (
    .in0(Input_Operand_1), .in1(Offset), .out(ALU_Operand_1), .sel(and_3_out[2]));
  Multiplexer #(.width(32), .enable("false")) multiplexer_2 (
    .in0(Input_Operand_2), .in1(32'h4), .out(ALU_Operand_2), .sel(and_3_out[2]));
  and and_3 (and_3_out[2], OPcode[5], not_5_out, not_6_out, OPcode[2], not_7_out, not_8_out);
  Multiplexer #(.select(3), .width(3), .enable("false")) multiplexer_3 (
    .in0(3'b010), .in1(3'b110), .in2(or_1_out), .in3(3'b100), .in4(3'b011), .in5(3'b011), .in6(3'b011),
    .in7(3'b011), .out(Result), .sel({and_3_out[2], ALUop}));
endmodule

module Debug_Register_Bank (
  input  Debug,
  input  Debug_Enable,
  input  [4:0] Debug_Write_Address,
  input  [31:0] Debug_Write_Data,
  input  [4:0] Read_1_Address,
  input  [4:0] Read_2_Address,
  input  [4:0] Write_Address,
  input  [31:0] Write_Data,
  input  Enable,
  input  Reset,
  input  Clock,
  output [31:0] Read_Data_1,
  output [31:0] Read_Data_2
);

  wire and_1_out, not_1_out, or_1_out;
  wire [4:0] multiplexer_1_out;
  wire [31:0] multiplexer_2_out;

  not not_1 (not_1_out, Debug);
  Multiplexer #(.width(5), .enable("false")) multiplexer_1 (
    .in0(Write_Address), .in1(Debug_Write_Address), .out(multiplexer_1_out), .sel(Debug));
  Multiplexer #(.width(32), .enable("false")) multiplexer_2 (
    .in0(Write_Data), .in1(Debug_Write_Data), .out(multiplexer_2_out), .sel(Debug));
  or or_1 (or_1_out, Debug_Enable, Enable);
  and and_1 (and_1_out, not_1_out, Reset);
  // Register_Bank register_bank_1: pin names not known; wires that end beside it: Read_1_Address, Read_2_Address, multiplexer_1_out, multiplexer_2_out, or_1_out, and_1_out, Clock, Read_Data_1, Read_Data_2
endmodule

module MIPS_Pipeline (
  input  Link,
  input  Jump,
  input  Manual,
  input  RegDst,
  input  [1:0] ALUop,
  input  ALUSrc,
  input  Branch,
  input  MemRead,
  input  MemWrite,
  input  MemToReg,
  input  RegWrite,
  input  Reset,
  output Link_2,
  output Jump_2,
  output Jump_3,
  output RegDst_2,
  output Branch_2,
  output MemtoReg_2,
  output [1:0] ALUop_2,
  output MemRead_2,
  output RegWrite_2,
  output ALUSrc_2,
  output MemWrite_2,
  output [31:0] High,
  output [31:0] Low
);

  wire alu_1_zero, alu_control_1_division, and_1_out, Clock, multiplexer_8_out, or_1_out, register_14_q,
       register_19_q, register_23_q, register_24_q, register_28_q;
  wire [1:0] register_11_q;
  wire [2:0] alu_control_1_result;
  wire [4:0] instruction_register_1__15_11, instruction_register_1__20_16, instruction_register_1__25_21,
       multiplexer_3_out, multiplexer_5_out, register_9_q, register_10_q, register_18_q, register_27_q;
  wire [5:0] instruction_register_1__31_26, OPcode, register_12_q, register_22_q;
  wire [10:0] control_1_out_13, register_3_q;
  wire [15:0] Im;
  wire [23:0] memory_input_1_result;
  wire [27:0] shl_26_28_1_out_2;
  wire [31:0] adder_1_out, adder_2_out, alu_1_remainder, alu_1_result, alu_control_1_alu_operand_1,
       alu_control_1_alu_operand_2, memory_output_1_result, merge_pc_1_out_3, multiplexer_1_out,
       multiplexer_2_out, multiplexer_4_out, multiplexer_6_out, multiplexer_7_out, PC_q, ram_1_data,
       ram_2_data, register_1_q, register_4_q, register_5_q, register_6_q, register_7_q, register_8_q,
       register_13_q, register_15_q, register_16_q, register_17_q, register_20_q, register_25_q,
       register_26_q, register_29_q, register_bank_1_read_data_1, register_bank_1_read_data_2,
       shl_32_1_out_2, sig_ext_1_out_2;

  Register #(.width(32)) PC (.D(multiplexer_1_out), .en(1'b1), .Q(PC_q), .clk(Clock), .clr(Reset));
  Clock u_Clock (.out(Clock));
  Multiplexer #(.width(32), .enable("false")) multiplexer_1 (
    .in0(adder_1_out), .in1(register_13_q), .out(multiplexer_1_out), .sel(or_1_out));
  Adder #(.width(32)) adder_1 (.a(32'h4), .b(PC_q), .out(adder_1_out));  // open: cin, cout
  Register #(.width(32)) register_1 (.D(adder_1_out), .en(1'b1), .Q(register_1_q), .clk(Clock), .clr(Reset));
  Instruction_Register instruction_register_1 (
    .in_1(ram_1_data), .Enable(1'b1), .Reset(Reset), .Clock(Clock), ._31_26(instruction_register_1__31_26),
    ._25_21(instruction_register_1__25_21), ._20_16(instruction_register_1__20_16),
    ._15_11(instruction_register_1__15_11), ._15_0(Im));
  RAM #(.addrWidth(24), .dataWidth(32), .bus("separate")) ram_1 (
    .addr(PC_q[25:2]), .data(ram_1_data), .str(1'b0), .sel(1'b1), .clk(Clock), .ld(1'b1), .clr(1'b0));  // open: din
  Control control_1 (
    .Link(Link), .Jump(Jump), .RegDst(RegDst), .ALUop(ALUop), .ALUSrc(ALUSrc), .Branch(Branch),
    .MemRead(MemRead), .MemWrite(MemWrite), .MemToReg(MemToReg), .RegWrite(RegWrite), .Debug(Manual),
    .OPCode(instruction_register_1__31_26), .out_13(control_1_out_13));
  merge_PC merge_pc_1 (.in_1(shl_26_28_1_out_2), .in_2(register_1_q[31:28]), .out_3(merge_pc_1_out_3));
  shl_26_28 shl_26_28_1 (
    .in_1({instruction_register_1__25_21, instruction_register_1__20_16, Im}), .out_2(shl_26_28_1_out_2));
  Register #(.width(6)) register_2 (.D(instruction_register_1__31_26), .en(1'b1), .Q(OPcode), .clk(Clock), .clr(Reset));
  Register_Bank register_bank_1 (
    .Read_1_Address(instruction_register_1__25_21), .Read_2_Address(instruction_register_1__20_16),
    .Write_Address(register_27_q), .Write_Data(memory_output_1_result), .Remainder(register_29_q),
    .Enable(multiplexer_8_out), .Reset(Reset), .Clock(Clock), .Division(register_28_q),
    .Read_Data_1(register_bank_1_read_data_1), .Read_Data_2(register_bank_1_read_data_2), .High(High),
    .Low(Low));
  sig_ext sig_ext_1 (.in_1(Im), .out_2(sig_ext_1_out_2));
  Register #(.width(11)) register_3 (
    .D(control_1_out_13), .en(1'b1),
    .Q({register_3_q[10], Jump_2, RegDst_2, ALUop_2, ALUSrc_2, register_3_q[4:0]}), .clk(Clock), .clr(Reset));
  Register #(.width(32)) register_4 (.D(merge_pc_1_out_3), .en(1'b1), .Q(register_4_q), .clk(Clock), .clr(Reset));
  Register #(.width(32)) register_5 (.D(register_1_q), .en(1'b1), .Q(register_5_q), .clk(Clock), .clr(Reset));
  shl_32 shl_32_1 (.in_1(register_8_q), .out_2(shl_32_1_out_2));
  Register #(.width(32)) register_6 (
    .D(register_bank_1_read_data_1), .en(1'b1), .Q(register_6_q), .clk(Clock), .clr(Reset));
  Register #(.width(32)) register_7 (
    .D(register_bank_1_read_data_2), .en(1'b1), .Q(register_7_q), .clk(Clock), .clr(Reset));
  Register #(.width(32)) register_8 (.D(sig_ext_1_out_2), .en(1'b1), .Q(register_8_q), .clk(Clock), .clr(Reset));
  Register #(.width(5)) register_9 (
    .D(instruction_register_1__20_16), .en(1'b1), .Q(register_9_q), .clk(Clock), .clr(Reset));
  Register #(.width(5)) register_10 (
    .D(instruction_register_1__15_11), .en(1'b1), .Q(register_10_q), .clk(Clock), .clr(Reset));
  Adder #(.width(32)) adder_2 (.a(register_5_q), .b(shl_32_1_out_2), .out(adder_2_out));  // open: cin, cout
  Multiplexer #(.width(32), .enable("false")) multiplexer_2 (
    .in0(register_7_q), .in1(register_8_q), .out(multiplexer_2_out), .sel(ALUSrc_2));
  ALU_Control alu_control_1 (
    .Input_Operand_1(register_6_q), .Input_Operand_2(multiplexer_2_out), .OPcode(OPcode),
    .Offset(register_8_q), .ALUop(ALUop_2), .Result(alu_control_1_result), .Division(alu_control_1_division),
    .ALU_Operand_1(alu_control_1_alu_operand_1), .ALU_Operand_2(alu_control_1_alu_operand_2));
  Multiplexer #(.width(5), .enable("false")) multiplexer_3 (
    .in0(register_9_q), .in1(register_10_q), .out(multiplexer_3_out), .sel(RegDst_2));
  Multiplexer #(.width(32), .enable("false")) multiplexer_4 (
    .in0(adder_2_out), .in1(register_4_q), .out(multiplexer_4_out), .sel(Jump_2));
  ALU alu_1 (
    .Operand_1(alu_control_1_alu_operand_1), .Operand_2(alu_control_1_alu_operand_2),
    .Control(alu_control_1_result), .Remainder(alu_1_remainder), .Zero(alu_1_zero), .Result(alu_1_result));
  Register #(.width(7)) register_11 (
    .D({register_3_q[10], Jump_2, register_3_q[4:0]}), .en(1'b1),
    .Q({Link_2, Jump_3, Branch_2, MemRead_2, MemWrite_2, register_11_q}), .clk(Clock), .clr(Reset));
  Register #(.width(6)) register_12 (.D(OPcode), .en(1'b1), .Q(register_12_q), .clk(Clock), .clr(Reset));
  Register #(.width(32)) register_13 (.D(multiplexer_4_out), .en(1'b1), .Q(register_13_q), .clk(Clock), .clr(Reset));
  Register #(.width(1)) register_14 (.D(alu_1_zero), .en(1'b1), .Q(register_14_q), .clk(Clock), .clr(Reset));
  Memory_Input memory_input_1 (.OPcode(register_12_q), .Address(register_15_q), .Result(memory_input_1_result));
  Register #(.width(32)) register_15 (.D(alu_1_result), .en(1'b1), .Q(register_15_q), .clk(Clock), .clr(Reset));
  Register #(.width(32)) register_16 (.D(register_7_q), .en(1'b1), .Q(register_16_q), .clk(Clock), .clr(Reset));
  Register #(.width(32)) register_17 (.D(register_5_q), .en(1'b1), .Q(register_17_q), .clk(Clock), .clr(Reset));
  Register #(.width(5)) register_18 (.D(multiplexer_3_out), .en(1'b1), .Q(register_18_q), .clk(Clock), .clr(Reset));
  Register #(.width(1)) register_19 (
    .D(alu_control_1_division), .en(1'b1), .Q(register_19_q), .clk(Clock), .clr(Reset));
  Register #(.width(32)) register_20 (.D(alu_1_remainder), .en(1'b1), .Q(register_20_q), .clk(Clock), .clr(Reset));
  Multiplexer #(.width(5), .enable("false")) multiplexer_5 (
    .in0(register_18_q), .in1({5{1'b1}}), .out(multiplexer_5_out), .sel(Link_2));
  or or_1 (or_1_out, Jump_3, and_1_out);
  and and_1 (and_1_out, Branch_2, register_14_q);
  Multiplexer #(.width(32), .enable("false")) multiplexer_6 (
    .in0(register_15_q), .in1(register_17_q), .out(multiplexer_6_out), .sel(Link_2));
  Register #(.width(2)) register_21 (
    .D(register_11_q), .en(1'b1), .Q({MemtoReg_2, RegWrite_2}), .clk(Clock), .clr(1'b0));
  Register #(.width(6)) register_22 (.D(register_12_q), .en(1'b1), .Q(register_22_q), .clk(Clock), .clr(Reset));
  Register #(.width(1)) register_23 (.D(Link_2), .en(1'b1), .Q(register_23_q), .clk(Clock), .clr(Reset));
  Register #(.width(1)) register_24 (.D(and_1_out), .en(1'b1), .Q(register_24_q), .clk(Clock), .clr(Reset));
  RAM #(.addrWidth(24), .dataWidth(32), .bus("separate")) ram_2 (
    .addr(memory_input_1_result), .din(register_16_q), .data(ram_2_data), .str(MemWrite_2), .sel(1'b1),
    .clk(Clock), .ld(MemRead_2), .clr(1'b0));
  Register #(.width(32)) register_25 (.D(ram_2_data), .en(1'b1), .Q(register_25_q), .clk(Clock), .clr(Reset));
  Register #(.width(32)) register_26 (.D(multiplexer_6_out), .en(1'b1), .Q(register_26_q), .clk(Clock), .clr(Reset));
  Register #(.width(5)) register_27 (.D(multiplexer_5_out), .en(1'b1), .Q(register_27_q), .clk(Clock), .clr(Reset));
  Register #(.width(1)) register_28 (.D(register_19_q), .en(1'b1), .Q(register_28_q), .clk(Clock), .clr(Reset));
  Register #(.width(32)) register_29 (.D(register_20_q), .en(1'b1), .Q(register_29_q), .clk(Clock), .clr(Reset));
  Multiplexer #(.width(32), .enable("false")) multiplexer_7 (
    .in0(register_26_q), .in1(register_25_q), .out(multiplexer_7_out), .sel(MemtoReg_2));
  Multiplexer #(.enable("false")) multiplexer_8 (
    .in0(RegWrite_2), .in1(register_24_q), .out(multiplexer_8_out), .sel(register_23_q));
  Memory_Output memory_output_1 (
    .OPcode(register_22_q), .Memory_Result(multiplexer_7_out), .Remainder(register_29_q),
    .Result(memory_output_1_result));

  // Notes on the sheet:
  //   Instruction Memory
  //   IF/ID
  //   :
  //   :
  //   :
  //   :
  //   IR
  //   :
  //   :
  //   :
  //   :
  //   :
  //   :
  //   :
  //   :
  //   inst 25-0
  //   conc PC 31_28
  //   shl_26_28
  //   Sig ext
  //   ID/EX
  //   :
  //   :
  //   :
  //   shl
  //   :
  //   :
  //   ALU Control
  //   ALU
  //   EX/MEM
  //   :
  //   :
  //   :
  //   :
  //   :
  //   :
  //   Data Memory
  //   MEM/WB
  //   :
  //   :
  //   :
  //   :
  //   :
  //   :
endmodule

module Control (
  input  Debug,
  input  [5:0] OPCode,
  input  Link,
  input  Jump,
  input  RegDst,
  input  [1:0] ALUop,
  input  ALUSrc,
  input  Branch,
  input  MemRead,
  input  MemWrite,
  input  MemToReg,
  input  RegWrite,
  output [10:0] out_13
);

  wire [10:0] rom_1_data;

  ROM #(.addrWidth(6), .dataWidth(11)) rom_1 (.addr(OPCode), .data(rom_1_data));  // open: sel
  Multiplexer #(.width(11), .enable("false")) multiplexer_1 (
    .in0(rom_1_data),
    .in1({Link, Jump, RegDst, ALUop, ALUSrc, Branch, MemRead, MemWrite, MemToReg, RegWrite}), .out(out_13),
    .sel(Debug));

  // Notes on the sheet:
  //   contents of rom_1 (hex, n*v repeats v):
  //   181 4f1 200 621 50 0 0 0 21 26*0 2b 2b 6*0 24
endmodule

module Operand_Calculator (
  input  [31:0] Operand_2,
  input  [5:0] OPcode,
  output [31:0] Result
);

  wire and_1_out, not_1_out, not_2_out, not_3_out, not_4_out;

  not not_1 (not_1_out, OPcode[4]);
  not not_2 (not_2_out, OPcode[3]);
  not not_3 (not_3_out, OPcode[1]);
  not not_4 (not_4_out, OPcode[0]);
  and and_1 (and_1_out, OPcode[5], not_1_out, not_2_out, OPcode[2], not_3_out, not_4_out);
  Multiplexer #(.width(32), .enable("false")) multiplexer_1 (
    .in0(Operand_2), .in1(32'h4), .out(Result), .sel(and_1_out));
endmodule

module Memory_Output (
  input  [5:0] OPcode,
  input  [31:0] Memory_Result,
  input  [31:0] Remainder,
  output [31:0] Result
);

  wire and_1_out, not_1_out, not_2_out, not_3_out, not_4_out;
  wire [7:0] bitselector_1_out;
  wire [31:0] bit_extender_1_out;

  not not_1 (not_1_out, OPcode[4]);
  not not_2 (not_2_out, OPcode[3]);
  not not_3 (not_3_out, OPcode[1]);
  not not_4 (not_4_out, OPcode[0]);
  BitSelector #(.width(32), .group(8)) bitselector_1 (
    .in(Memory_Result), .out(bitselector_1_out), .sel(Remainder[1:0]));
  assign bit_extender_1_out = {{24{1'b0}}, bitselector_1_out};  // Bit_Extender bit_extender_1
  and and_1 (and_1_out, OPcode[5], not_1_out, not_2_out, OPcode[2], not_3_out, not_4_out);
  Multiplexer #(.width(32), .enable("false")) multiplexer_1 (
    .in0(Memory_Result), .in1(bit_extender_1_out), .out(Result), .sel(and_1_out));
endmodule

module Memory_Input (
  input  [5:0] OPcode,
  input  [31:0] Address,
  output [23:0] Result
);

  wire and_1_out, not_1_out, not_2_out, not_3_out, not_4_out;

  not not_1 (not_1_out, OPcode[4]);
  not not_2 (not_2_out, OPcode[3]);
  not not_3 (not_3_out, OPcode[1]);
  not not_4 (not_4_out, OPcode[0]);
  and and_1 (and_1_out, OPcode[5], not_1_out, not_2_out, OPcode[2], not_3_out, not_4_out);
  Multiplexer #(.width(24), .enable("false")) multiplexer_1 (
    .in0(Address[25:2]), .in1(Address[23:0]), .out(Result), .sel(and_1_out));
endmodule
